// Logisim project control-logic.circ as structural Verilog: 1 circuit, main circuit control_logic
module control_logic (
  input  [31:0] Instruction,
  input  BrEq,
  input  BrLt,
  output PCSel,
  output RegWEn,
  output [2:0] ImmSel,
  output BrUn,
  output ASel,
  output BSel,
  output [3:0] ALUSel,
  output MemWEn,
  output [1:0] WBSel
);

  wire and_1_out, and_2_out, and_3_out, and_4_out, and_5_out, and_24_out, and_32_out, and_33_out, and_34_out,
       comparator_10_eq, comparator_11_eq, comparator_12_eq, comparator_13_eq, comparator_14_eq,
       comparator_15_eq, comparator_16_eq, comparator_17_eq, comparator_18_eq, comparator_19_eq,
       comparator_20_eq, comparator_21_eq, comparator_22_eq, comparator_23_eq, comparator_24_eq,
       comparator_25_eq, comparator_26_eq, comparator_27_eq, comparator_28_eq, comparator_29_eq,
       comparator_30_eq, comparator_31_eq, comparator_32_eq, comparator_33_eq, comparator_34_eq,
       comparator_35_eq, comparator_36_eq, comparator_37_eq, comparator_38_eq, comparator_39_eq,
       comparator_40_eq, comparator_41_eq, comparator_42_eq, comparator_43_eq, comparator_44_eq,
       comparator_45_eq, instadd, instaddi, instand, instandi, instauipc, instB, instBEQ, instBGE, instBGEU,
       instBLT, instBLTU, instBNE, instI, instjal, instjalr, instlb, instlh, instload, instlui, instlw,
       instmul, instmulh, instmulhu, instor, instori, instR, instS, instsb, instsh, instsll, instslli,
       instslt, instslti, instsra, instsrai, instsrl, instsrli, instsub, instsw, instxor, instxori,
       not_1_out, not_2_out, or_1_out;
  wire [5:0] ROMInput;
  wire [15:14] rom_1_data;

  ROM #(.addrWidth(6), .dataWidth(16)) rom_1 (
    .addr(ROMInput), .data({rom_1_data, WBSel, MemWEn, ALUSel, BSel, ASel, BrUn, ImmSel, RegWEn}));
  Priority_Encoder #(.select_enc(6)) priority_encoder_1 (
    .in0(instadd), .in1(instmul), .in2(instsub), .in3(instsll), .in4(instmulh), .in5(instmulhu),
    .in6(instslt), .in7(instxor), .in8(instsrl), .in9(instsra), .in10(instor), .in11(instand), .in12(instlb),
    .in13(instlh), .in14(instlw), .in15(instaddi), .in16(instslli), .in17(instslti), .in18(instxori),
    .in19(instsrli), .in20(instsrai), .in21(instori), .in22(instandi), .in23(instsb), .in24(instsh),
    .in25(instsw), .in26(instBEQ), .in27(instBNE), .in28(instBLT), .in29(instBGE), .in30(instBLTU),
    .in31(instBGEU), .in32(instauipc), .in33(instlui), .in34(instjal), .in35(instjalr), .out(ROMInput));  // open: in36, in37, in38, in39, in40, in41, in42, in43, in44, in45, in46, in47, in48, in49, in50, in51, in52, in53, in54, in55, in56, in57, in58, in59, in60, in61, in62, in63, gs, en_out, en_in
  or or_1 (or_1_out, instBGE, instBGEU);
  not not_1 (not_1_out, BrLt);
  and and_1 (and_1_out, or_1_out, not_1_out);
  and and_2 (and_2_out, instBLT, BrLt);
  and and_3 (and_3_out, instBLTU, BrLt);
  Comparator #(.width(7)) comparator_1 (.a(Instruction[6:0]), .b(7'b1100011), .eq(instB));  // open: gt, lt
  Comparator #(.width(7)) comparator_2 (.a(Instruction[6:0]), .b(7'b0100011), .eq(instS));  // open: gt, lt
  Comparator #(.width(7)) comparator_3 (.a(Instruction[6:0]), .b(7'b0110011), .eq(instR));  // open: gt, lt
  Comparator #(.width(7)) comparator_4 (.a(Instruction[6:0]), .b(7'b0010011), .eq(instI));  // open: gt, lt
  Comparator #(.width(7)) comparator_5 (.a(Instruction[6:0]), .b(7'b0000011), .eq(instload));  // open: gt, lt
  Comparator #(.width(7)) comparator_6 (.a(Instruction[6:0]), .b(7'b1101111), .eq(instjal));  // open: gt, lt
  or or_2 (PCSel, and_1_out, and_3_out, and_2_out, and_4_out, and_5_out, instjal, instjalr);
  Comparator #(.width(7)) comparator_7 (.a(Instruction[6:0]), .b(7'b1100111), .eq(instjalr));  // open: gt, lt
  Comparator #(.width(7)) comparator_8 (.a(Instruction[6:0]), .b(7'b0010111), .eq(instauipc));  // open: gt, lt
  Comparator #(.width(7)) comparator_9 (.a(Instruction[6:0]), .b(7'b0110111), .eq(instlui));  // open: gt, lt
  not not_2 (not_2_out, BrEq);
  and and_4 (and_4_out, instBEQ, BrEq);
  and and_5 (and_5_out, instBNE, not_2_out);
  Comparator #(.width(3)) comparator_10 (.a(Instruction[14:12]), .b(3'b000), .eq(comparator_10_eq));  // open: gt, lt
  Comparator #(.width(3)) comparator_11 (.a(Instruction[14:12]), .b(3'b001), .eq(comparator_11_eq));  // open: gt, lt
  Comparator #(.width(3)) comparator_12 (.a(Instruction[14:12]), .b(3'b100), .eq(comparator_12_eq));  // open: gt, lt
  Comparator #(.width(3)) comparator_13 (.a(Instruction[14:12]), .b(3'b101), .eq(comparator_13_eq));  // open: gt, lt
  Comparator #(.width(3)) comparator_14 (.a(Instruction[14:12]), .b(3'b110), .eq(comparator_14_eq));  // open: gt, lt
  Comparator #(.width(3)) comparator_15 (.a(Instruction[14:12]), .b(3'b111), .eq(comparator_15_eq));  // open: gt, lt
  and and_6 (instBEQ, instB, comparator_10_eq);
  and and_7 (instBNE, instB, comparator_11_eq);
  and and_8 (instBLT, instB, comparator_12_eq);
  and and_9 (instBGE, instB, comparator_13_eq);
  and and_10 (instBLTU, instB, comparator_14_eq);
  and and_11 (instBGEU, instB, comparator_15_eq);
  Comparator #(.width(3)) comparator_16 (.a(Instruction[14:12]), .b(3'b000), .eq(comparator_16_eq));  // open: gt, lt
  Comparator #(.width(3)) comparator_17 (.a(Instruction[14:12]), .b(3'b001), .eq(comparator_17_eq));  // open: gt, lt
  Comparator #(.width(3)) comparator_18 (.a(Instruction[14:12]), .b(3'b010), .eq(comparator_18_eq));  // open: gt, lt
  Comparator #(.width(3)) comparator_19 (.a(Instruction[14:12]), .b(3'b000), .eq(comparator_19_eq));  // open: gt, lt
  Comparator #(.width(3)) comparator_20 (.a(Instruction[14:12]), .b(3'b001), .eq(comparator_20_eq));  // open: gt, lt
  Comparator #(.width(3)) comparator_21 (.a(Instruction[14:12]), .b(3'b010), .eq(comparator_21_eq));  // open: gt, lt
  and and_12 (instsb, instS, comparator_16_eq);
  and and_13 (instsh, instS, comparator_17_eq);
  and and_14 (instsw, instS, comparator_18_eq);
  and and_15 (instlb, instload, comparator_19_eq);
  and and_16 (instlh, instload, comparator_20_eq);
  and and_17 (instlw, instload, comparator_21_eq);
  Comparator #(.width(3)) comparator_22 (.a(Instruction[14:12]), .b(3'b000), .eq(comparator_22_eq));  // open: gt, lt
  Comparator #(.width(3)) comparator_23 (.a(Instruction[14:12]), .b(3'b001), .eq(comparator_23_eq));  // open: gt, lt
  Comparator #(.width(3)) comparator_24 (.a(Instruction[14:12]), .b(3'b010), .eq(comparator_24_eq));  // open: gt, lt
  Comparator #(.width(3)) comparator_25 (.a(Instruction[14:12]), .b(3'b100), .eq(comparator_25_eq));  // open: gt, lt
  Comparator #(.width(3)) comparator_26 (.a(Instruction[14:12]), .b(3'b110), .eq(comparator_26_eq));  // open: gt, lt
  Comparator #(.width(3)) comparator_27 (.a(Instruction[14:12]), .b(3'b111), .eq(comparator_27_eq));  // open: gt, lt
  Comparator #(.width(3)) comparator_28 (.a(Instruction[14:12]), .b(3'b101), .eq(comparator_28_eq));  // open: gt, lt
  and and_18 (instaddi, instI, comparator_22_eq);
  and and_19 (instslli, instI, comparator_23_eq);
  and and_20 (instslti, instI, comparator_24_eq);
  and and_21 (instxori, instI, comparator_25_eq);
  and and_22 (instori, instI, comparator_26_eq);
  and and_23 (instandi, instI, comparator_27_eq);
  Comparator #(.width(7)) comparator_29 (.a(Instruction[31:25]), .b({7{1'b0}}), .eq(comparator_29_eq));  // open: gt, lt
  and and_24 (and_24_out, instI, comparator_28_eq);
  Comparator #(.width(7)) comparator_30 (
    .a(Instruction[31:25]), .b(7'b0100000), .eq(comparator_30_eq));  // open: gt, lt
  and and_25 (instsrli, comparator_29_eq, and_24_out);
  and and_26 (instsrai, and_24_out, comparator_30_eq);
  Comparator #(.width(3)) comparator_31 (.a(Instruction[14:12]), .b(3'b011), .eq(comparator_31_eq));  // open: gt, lt
  Comparator #(.width(3)) comparator_32 (.a(Instruction[14:12]), .b(3'b010), .eq(comparator_32_eq));  // open: gt, lt
  Comparator #(.width(3)) comparator_33 (.a(Instruction[14:12]), .b(3'b100), .eq(comparator_33_eq));  // open: gt, lt
  Comparator #(.width(3)) comparator_34 (.a(Instruction[14:12]), .b(3'b110), .eq(comparator_34_eq));  // open: gt, lt
  Comparator #(.width(3)) comparator_35 (.a(Instruction[14:12]), .b(3'b111), .eq(comparator_35_eq));  // open: gt, lt
  and and_27 (instmulhu, instR, comparator_31_eq);
  and and_28 (instslt, instR, comparator_32_eq);
  and and_29 (instxor, instR, comparator_33_eq);
  and and_30 (instor, instR, comparator_34_eq);
  and and_31 (instand, instR, comparator_35_eq);
  Comparator #(.width(3)) comparator_36 (.a(Instruction[14:12]), .b(3'b000), .eq(comparator_36_eq));  // open: gt, lt
  Comparator #(.width(3)) comparator_37 (.a(Instruction[14:12]), .b(3'b101), .eq(comparator_37_eq));  // open: gt, lt
  Comparator #(.width(3)) comparator_38 (.a(Instruction[14:12]), .b(3'b001), .eq(comparator_38_eq));  // open: gt, lt
  and and_32 (and_32_out, instR, comparator_36_eq);
  Comparator #(.width(7)) comparator_39 (
    .a(Instruction[31:25]), .b(7'b0100000), .eq(comparator_39_eq));  // open: gt, lt
  and and_33 (and_33_out, instR, comparator_37_eq);
  and and_34 (and_34_out, instR, comparator_38_eq);
  Comparator #(.width(7)) comparator_40 (.a(Instruction[31:25]), .b({7{1'b0}}), .eq(comparator_40_eq));  // open: gt, lt
  Comparator #(.width(7)) comparator_41 (
    .a(Instruction[31:25]), .b(7'b0000001), .eq(comparator_41_eq));  // open: gt, lt
  Comparator #(.width(7)) comparator_42 (.a(Instruction[31:25]), .b({7{1'b0}}), .eq(comparator_42_eq));  // open: gt, lt
  Comparator #(.width(7)) comparator_43 (
    .a(Instruction[31:25]), .b(7'b0100000), .eq(comparator_43_eq));  // open: gt, lt
  Comparator #(.width(7)) comparator_44 (.a(Instruction[31:25]), .b({7{1'b0}}), .eq(comparator_44_eq));  // open: gt, lt
  Comparator #(.width(7)) comparator_45 (
    .a(Instruction[31:25]), .b(7'b0000001), .eq(comparator_45_eq));  // open: gt, lt
  and and_35 (instadd, comparator_40_eq, and_32_out);
  and and_36 (instmul, and_32_out, comparator_41_eq);
  and and_37 (instsub, and_32_out, comparator_39_eq);
  and and_38 (instsrl, comparator_42_eq, and_33_out);
  and and_39 (instsra, and_33_out, comparator_43_eq);
  and and_40 (instsll, comparator_44_eq, and_34_out);
  and and_41 (instmulh, and_34_out, comparator_45_eq);

  // Other names for the same wires on the sheet: opcode[6:0] = Instruction[6:0]; f3[2:0] = Instruction[14:12];
  //   f7[6:0] = Instruction[31:25]

  // Notes on the sheet:
  //   INPUTS to your circuit
  //   contents of rom_1 (hex, n*v repeats v):
  //   1001 1401 1601 1081 1481 1581 1101 1201 1281 1681 1301 1381 41 41 41 1041 10c1 1141 1241 12c1 16c1
  //   1341 13c1 842 842 842 4*64 74 74 1067 17e7 2069 2041
  //   ROM FOR CONTROL LOGIC
  //   DON'T CHANGE THE LOCATIONS OF THE INPUTS AND OUTPUTS!
  //   This is only if you choose to do the ROM option
  //   OUTPUT from your circuit
  //   B-Type Instructions
  //   B-Type Instructions
  //   I-Type Instructions
  //   R-Type Instructions
endmodule
