// Logisim project cpu.circ as structural Verilog: 1 circuit, main circuit cpu
module cpu (
  input  clk,
  input  [31:0] Instruction,
  input  [31:0] MemReadData,
  output [31:0] MemAddress,
  output [31:0] ProgramCounter,
  output [31:0] ra,
  output [31:0] sp,
  output [31:0] t0,
  output [31:0] t1,
  output [31:0] t2,
  output [31:0] s0,
  output [31:0] s1,
  output [31:0] a0,
  output [3:0] MemWriteMask,
  output [31:0] MemWriteData
);

  wire ASelTunnel, BrEqTunnel, BrLtTunnel, BSelTunnel, comparator_1_eq, comparator_2_eq,
       control_logic_1_brun, control_logic_1_memwen, control_logic_1_pcsel, control_logic_1_regwen, or_1_out;
  wire [1:0] control_logic_1_wbsel;
  wire [2:0] control_logic_1_immsel;
  wire [3:0] control_logic_1_alusel, partial_store_1_memwritemask;
  wire [6:0] opcode;
  wire [31:0] adder_1_out, adder_2_out, ALUResult, imm_gen_1_immediate, memwbdata, multiplexer_1_out,
       multiplexer_2_out, multiplexer_3_out, multiplexer_4_out, partial_load_1_datatoreg,
       partial_store_1_datatomem, ProgramCounter2, ProgramCounterPlus4, regfile_1_readdata1, rs2data, WBdata;
  wire [31:7] pinstruction;

  Multiplexer #(.width(32)) multiplexer_1 (
    .in0(Instruction), .in1(32'h13), .out(multiplexer_1_out), .sel(control_logic_1_pcsel));
  Register #(.width(32)) register_1 (.D(ProgramCounter), .clk(clk), .Q(ProgramCounter2));  // open: en, clr
  Adder #(.width(32)) adder_1 (.a(ProgramCounter), .b(32'h4), .out(adder_1_out));  // open: cin, cout
  Multiplexer #(.width(32)) multiplexer_2 (
    .in0(adder_1_out), .in1(ALUResult), .out(multiplexer_2_out), .sel(control_logic_1_pcsel));
  Register #(.width(32)) register_2 (.D(multiplexer_1_out), .clk(clk), .Q({pinstruction, opcode}));  // open: en, clr
  Register #(.width(32)) PC (.D(multiplexer_2_out), .clk(clk), .Q(ProgramCounter));  // open: en, clr
  // Probe on {pinstruction, opcode}
  Register #(.width(32)) register_3 (.D(adder_1_out), .clk(clk), .Q(ProgramCounterPlus4));  // open: en, clr
  control_logic control_logic_1 (
    .Instruction({pinstruction, opcode}), .BrEq(BrEqTunnel), .BrLt(BrLtTunnel),
    .PCSel(control_logic_1_pcsel), .RegWEn(control_logic_1_regwen), .ImmSel(control_logic_1_immsel),
    .BrUn(control_logic_1_brun), .ASel(ASelTunnel), .BSel(BSelTunnel), .ALUSel(control_logic_1_alusel),
    .MemWEn(control_logic_1_memwen), .WBSel(control_logic_1_wbsel));
  regfile regfile_1 (
    .ReadIndex1(pinstruction[19:15]), .ReadIndex2(pinstruction[24:20]), .WriteIndex(pinstruction[11:7]),
    .WriteData(WBdata), .RegWEn(control_logic_1_regwen), .clk(clk), .ra(ra), .sp(sp), .t0(t0), .t1(t1),
    .t2(t2), .s0(s0), .s1(s1), .a0(a0), .ReadData1(regfile_1_readdata1), .ReadData2(rs2data));
  imm_gen imm_gen_1 (
    .Instruction({pinstruction, opcode}), .ImmSel(control_logic_1_immsel), .Immediate(imm_gen_1_immediate));
  // Probe on multiplexer_3_out
  Multiplexer #(.width(32)) multiplexer_3 (
    .in0(regfile_1_readdata1), .in1(ProgramCounter2), .out(multiplexer_3_out), .sel(ASelTunnel));
  // Probe on rs2data
  // Probe on multiplexer_4_out
  Multiplexer #(.width(32)) multiplexer_4 (
    .in0(rs2data), .in1(imm_gen_1_immediate), .out(multiplexer_4_out), .sel(BSelTunnel));
  Adder #(.width(32)) adder_2 (.a(ProgramCounter2), .b(32'h4), .out(adder_2_out));  // open: cin, cout
  alu alu_1 (.A(multiplexer_3_out), .B(multiplexer_4_out), .ALUSel(control_logic_1_alusel), .ALUResult(ALUResult));
  branch_comp branch_comp_1 (
    .BrData1(regfile_1_readdata1), .BrData2(rs2data), .BrUn(control_logic_1_brun), .BrEq(BrEqTunnel),
    .BrLt(BrLtTunnel));
  Multiplexer #(.select(2), .width(32)) multiplexer_5 (
    .in0(memwbdata), .in1(ALUResult), .in2(ProgramCounterPlus4), .out(WBdata), .sel(control_logic_1_wbsel));  // open: in3
  Comparator #(.width(7)) comparator_1 (.a(opcode), .b(7'b0000011), .eq(comparator_1_eq));  // open: gt, lt
  Comparator #(.width(7)) comparator_2 (.a(opcode), .b(7'b0100011), .eq(comparator_2_eq));  // open: gt, lt
  Demultiplexer #(.width(32)) demultiplexer_1 (.out1(MemAddress), .in(ALUResult), .sel(or_1_out));  // open: out0
  or or_1 (or_1_out, comparator_1_eq, comparator_2_eq);
  Demultiplexer #(.width(4)) demultiplexer_2 (
    .out1(MemWriteMask), .in(partial_store_1_memwritemask), .sel(comparator_2_eq));  // open: out0
  partial_store partial_store_1 (
    .Instruction({pinstruction, opcode}), .MemAddress(MemAddress), .DataFromReg(rs2data),
    .MemWEn(control_logic_1_memwen), .MemWriteMask(partial_store_1_memwritemask),
    .DataToMem(partial_store_1_datatomem));
  Demultiplexer #(.width(32)) demultiplexer_3 (
    .out1(MemWriteData), .in(partial_store_1_datatomem), .sel(comparator_2_eq));  // open: out0
  partial_load partial_load_1 (
    .Instruction({pinstruction, opcode}), .MemAddress(MemAddress), .DataFromMem(MemReadData),
    .DataToReg(partial_load_1_datatoreg));
  Multiplexer #(.width(32)) multiplexer_6 (
    .in0({32{1'b0}}), .in1(partial_load_1_datatoreg), .out(memwbdata), .sel(comparator_1_eq));

  // Other names for the same wires on the sheet: pinstruction[6:0] = opcode

  // Notes on the sheet:
  //   To IMEM
  //   IMEM (do **NOT** move this)
  //   From IMEM
  //   Inputs/Outputs for testing. Do **NOT** move these.
  //   It is OK to move the PC, RegFile, ALU, MEM, Branch Comp, Imm Gen, Partial Load, Partial Store and Control Logic to wherever is most convenient for you when constructing your CPU, and to delete this text
  //   To DMEM
  //   DMEM (do **NOT** move this)
  //   From DMEM
endmodule
