// Logisim project imm-gen.circ as structural Verilog: 1 circuit, main circuit imm_gen
module imm_gen (
  input  [31:0] Instruction,
  input  [2:0] ImmSel,
  output [31:0] Immediate
);

  wire [4:0] demultiplexer_1_out1_2;
  wire [5:0] demultiplexer_1_out1_3;
  wire [11:0] bit_extender_3_out, demultiplexer_1_out0_2;
  wire [19:0] bit_extender_4_out, demultiplexer_1_out0;
  wire [20:0] bit_extender_2_out;
  wire [31:0] bit_extender_1_out, demultiplexer_1_out1, demultiplexer_1_out2, demultiplexer_1_out3,
       demultiplexer_1_out4;

  Demultiplexer #(.select(3), .width(32)) demultiplexer_1 (
    .out0({demultiplexer_1_out0_2, demultiplexer_1_out0}),
    .out1({demultiplexer_1_out1[31], demultiplexer_1_out1_3, demultiplexer_1_out1[24:12], demultiplexer_1_out1_2, demultiplexer_1_out1[6:0]}),
    .out2(demultiplexer_1_out2), .out3(demultiplexer_1_out3), .out4(demultiplexer_1_out4), .in(Instruction),
    .sel(ImmSel));  // open: out5, out6, out7
  // Buffer buffer_1 is placed but not wired
  assign bit_extender_1_out = {{20{demultiplexer_1_out0_2[11]}}, demultiplexer_1_out0_2};  // Bit_Extender bit_extender_1
  assign bit_extender_2_out = {{20{demultiplexer_1_out1[31]}}, demultiplexer_1_out1[31]};  // Bit_Extender bit_extender_2
  assign bit_extender_3_out = {{11{demultiplexer_1_out4[31]}}, demultiplexer_1_out4[31]};  // Bit_Extender bit_extender_3
  assign bit_extender_4_out = {{19{demultiplexer_1_out2[31]}}, demultiplexer_1_out2[31]};  // Bit_Extender bit_extender_4
  Multiplexer #(.select(3), .width(32)) multiplexer_1 (
    .in0(bit_extender_1_out), .in1({bit_extender_2_out, demultiplexer_1_out1_3, demultiplexer_1_out1_2}),
    .in2({bit_extender_4_out, demultiplexer_1_out2[7], demultiplexer_1_out2[30:25], demultiplexer_1_out2[11:8], 1'b0}),
    .in3({demultiplexer_1_out3[31:12], {12{1'b0}}}),
    .in4({bit_extender_3_out, demultiplexer_1_out4[19:12], demultiplexer_1_out4[20], demultiplexer_1_out4[30:21], 1'b0}),
    .out(Immediate), .sel(ImmSel));  // open: in5, in6, in7

  // Notes on the sheet:
  //   INPUTS to your circuit
  //   0b000 ---> I
  //   0b001 ---> S
  //   0b010 ---> B
  //   0b011 ---> U
  //   0b100 ---> J
  //   DON'T CHANGE THE LOCATIONS OF THE INPUTS AND OUTPUTS!
  //   OUTPUT from your circuit
endmodule
