// Logisim project partial-load.circ as structural Verilog: 1 circuit, main circuit partial_load
module partial_load (
  input  [31:0] Instruction,
  input  [31:0] MemAddress,
  input  [31:0] DataFromMem,
  output [31:0] DataToReg
);

  wire [24:0] bit_extender_4_out;
  wire [31:0] bit_extender_2_out, bit_extender_3_out, bit_extender_5_out, bit_extender_6_out,
       bit_extender_7_out, demultiplexer_1_out2, demultiplexer_2_out0_2, demultiplexer_2_out1,
       demultiplexer_2_out2, demultiplexer_3_out0, demultiplexer_3_out1, demultiplexer_3_out2,
       demultiplexer_3_out3, lbdata, lbdatain, lhdata, lhdatain;
  wire [31:15] demultiplexer_2_out0;

  Demultiplexer #(.select(3), .width(32)) demultiplexer_1 (
    .out0(lbdatain), .out1(lhdatain), .out2(demultiplexer_1_out2), .in(DataFromMem), .sel(Instruction[14:12]));  // open: out3, out4, out5, out6, out7
  Demultiplexer #(.select(2), .width(32)) demultiplexer_2 (
    .out0({demultiplexer_2_out0, demultiplexer_2_out0_2[14:0]}), .out1(demultiplexer_2_out1),
    .out2(demultiplexer_2_out2), .in(lhdatain), .sel(MemAddress[1:0]));  // open: out3
  Multiplexer #(.select(3), .width(32)) multiplexer_1 (
    .in0(lbdata), .in1(lhdata), .in2(demultiplexer_1_out2), .out(DataToReg), .sel(Instruction[14:12]));  // open: in3, in4, in5, in6, in7
  assign demultiplexer_2_out0_2[31:15] = {{16{demultiplexer_2_out0[15]}}, demultiplexer_2_out0[15]};  // Bit_Extender bit_extender_1
  assign bit_extender_2_out = {{16{demultiplexer_2_out1[23]}}, demultiplexer_2_out1[23:8]};  // Bit_Extender bit_extender_2
  assign bit_extender_3_out = {{16{demultiplexer_2_out2[31]}}, demultiplexer_2_out2[31:16]};  // Bit_Extender bit_extender_3
  Multiplexer #(.select(2), .width(32)) multiplexer_2 (
    .in0(demultiplexer_2_out0_2), .in1(bit_extender_2_out), .in2(bit_extender_3_out), .out(lhdata),
    .sel(MemAddress[1:0]));  // open: in3
  Demultiplexer #(.select(2), .width(32)) demultiplexer_3 (
    .out0(demultiplexer_3_out0), .out1(demultiplexer_3_out1), .out2(demultiplexer_3_out2),
    .out3(demultiplexer_3_out3), .in(lbdatain), .sel(MemAddress[1:0]));
  assign bit_extender_4_out = {{24{demultiplexer_3_out0[7]}}, demultiplexer_3_out0[7]};  // Bit_Extender bit_extender_4
  assign bit_extender_5_out = {{24{demultiplexer_3_out1[15]}}, demultiplexer_3_out1[15:8]};  // Bit_Extender bit_extender_5
  assign bit_extender_6_out = {{24{demultiplexer_3_out2[23]}}, demultiplexer_3_out2[23:16]};  // Bit_Extender bit_extender_6
  assign bit_extender_7_out = {{24{demultiplexer_3_out3[31]}}, demultiplexer_3_out3[31:24]};  // Bit_Extender bit_extender_7
  Multiplexer #(.select(2), .width(32)) multiplexer_3 (
    .in0({bit_extender_4_out, demultiplexer_3_out0[6:0]}), .in1(bit_extender_5_out),
    .in2(bit_extender_6_out), .in3(bit_extender_7_out), .out(lbdata), .sel(MemAddress[1:0]));

  // Other names for the same wires on the sheet: b2[1:0] = MemAddress[1:0]

  // Notes on the sheet:
  //   INPUTS to your circuit
  //   DON'T CHANGE THE LOCATIONS OF THE INPUTS AND OUTPUTS!
  //   OUTPUT from your circuit
endmodule
