// Logisim project partial-store.circ as structural Verilog: 1 circuit, main circuit partial_store
module partial_store (
  input  [31:0] Instruction,
  input  [31:0] MemAddress,
  input  [31:0] DataFromReg,
  input  MemWEn,
  output [3:0] MemWriteMask,
  output [31:0] DataToMem
);

  wire [3:0] demultiplexer_1_out2, demultiplexer_5_out1, demultiplexer_6_out0, demultiplexer_6_out1,
       demultiplexer_6_out2, demultiplexer_6_out3, demultiplexer_7_out0, demultiplexer_7_out2,
       multiplexer_2_out, sbmaskin, sbmaskout, shifter_1_out, shifter_2_out, shmaskin, shmaskout;
  wire [31:0] demultiplexer_2_out2, demultiplexer_4_out0, demultiplexer_4_out1, demultiplexer_4_out2,
       demultiplexer_4_out3, demultiplexer_8_out0, demultiplexer_8_out2, multiplexer_1_out, sbinput, sbout,
       shinput, shout;

  Demultiplexer #(.select(3), .width(4)) demultiplexer_1 (
    .out0(sbmaskin), .out1(shmaskin), .out2(demultiplexer_1_out2), .in(4'b1111), .sel(Instruction[14:12]));  // open: out3, out4, out5, out6, out7
  Demultiplexer #(.select(3), .width(32)) demultiplexer_2 (
    .out0(sbinput), .out1(shinput), .out2(demultiplexer_2_out2), .in(DataFromReg), .sel(Instruction[14:12]));  // open: out3, out4, out5, out6, out7
  Multiplexer #(.select(3), .width(32)) multiplexer_1 (
    .in0(sbout), .in1(shout), .in2(demultiplexer_2_out2), .out(multiplexer_1_out), .sel(Instruction[14:12]));  // open: in3, in4, in5, in6, in7
  Multiplexer #(.select(3), .width(4)) multiplexer_2 (
    .in0(sbmaskout), .in1(shmaskout), .in2(demultiplexer_1_out2), .out(multiplexer_2_out),
    .sel(Instruction[14:12]));  // open: in3, in4, in5, in6, in7
  Demultiplexer #(.width(32)) demultiplexer_3 (.out1(DataToMem), .in(multiplexer_1_out), .sel(MemWEn));  // open: out0
  Demultiplexer #(.select(2), .width(32)) demultiplexer_4 (
    .out0(demultiplexer_4_out0), .out1(demultiplexer_4_out1), .out2(demultiplexer_4_out2),
    .out3(demultiplexer_4_out3), .in(sbinput), .sel(MemAddress[1:0]));
  Demultiplexer #(.width(4)) demultiplexer_5 (
    .out1(demultiplexer_5_out1), .in(multiplexer_2_out), .sel(MemWEn));  // open: out0
  Multiplexer #(.width(4)) multiplexer_3 (.in0(4'b0000), .in1(demultiplexer_5_out1), .out(MemWriteMask), .sel(MemWEn));
  Multiplexer #(.select(2), .width(32)) multiplexer_4 (
    .in0({{24{1'b0}}, demultiplexer_4_out0[7:0]}), .in1({{16{1'b0}}, demultiplexer_4_out1[7:0], {8{1'b0}}}),
    .in2({{8{1'b0}}, demultiplexer_4_out2[7:0], {16{1'b0}}}), .in3({demultiplexer_4_out3[7:0], {24{1'b0}}}),
    .out(sbout), .sel(MemAddress[1:0]));
  Demultiplexer #(.select(2), .width(4)) demultiplexer_6 (
    .out0(demultiplexer_6_out0), .out1(demultiplexer_6_out1), .out2(demultiplexer_6_out2),
    .out3(demultiplexer_6_out3), .in(sbmaskin), .sel(MemAddress[1:0]));
  Demultiplexer #(.select(2), .width(4)) demultiplexer_7 (
    .out0(demultiplexer_7_out0), .out2(demultiplexer_7_out2), .in(shmaskin), .sel(MemAddress[1:0]));  // open: out1, out3
  Shifter #(.shift("lr"), .width(4)) shifter_1 (.in(demultiplexer_7_out0), .\dist (2'b10), .out(shifter_1_out));
  Shifter #(.width(4)) shifter_2 (.in(demultiplexer_7_out2), .\dist (2'b10), .out(shifter_2_out));
  Demultiplexer #(.select(2), .width(32)) demultiplexer_8 (
    .out0(demultiplexer_8_out0), .out2(demultiplexer_8_out2), .in(shinput), .sel(MemAddress[1:0]));  // open: out1, out3
  Multiplexer #(.select(2), .width(4)) multiplexer_5 (
    .in0({3'b000, demultiplexer_6_out0[0]}), .in1({2'b00, demultiplexer_6_out1[0], 1'b0}),
    .in2({1'b0, demultiplexer_6_out2[0], 2'b00}), .in3({demultiplexer_6_out3[0], 3'b000}), .out(sbmaskout),
    .sel(MemAddress[1:0]));
  Multiplexer #(.select(2), .width(4)) multiplexer_6 (
    .in0(shifter_1_out), .in2(shifter_2_out), .out(shmaskout), .sel(MemAddress[1:0]));  // open: in1, in3
  Multiplexer #(.select(2), .width(32)) multiplexer_7 (
    .in0({{16{1'b0}}, demultiplexer_8_out0[15:0]}), .in2({demultiplexer_8_out2[15:0], {16{1'b0}}}),
    .out(shout), .sel(MemAddress[1:0]));  // open: in1, in3

  // Other names for the same wires on the sheet: func3[2:0] = Instruction[14:12]; b2[1:0] = MemAddress[1:0]

  // Notes on the sheet:
  //   INPUTS to your circuit
  //   DON'T CHANGE THE LOCATIONS OF THE INPUTS AND OUTPUTS!
  //   OUTPUT from your circuit
endmodule
