// Logisim project regfile.circ as structural Verilog: 1 circuit, main circuit regfile
module regfile (
  input  [4:0] ReadIndex1,
  input  [4:0] ReadIndex2,
  input  [4:0] WriteIndex,
  input  [31:0] WriteData,
  input  RegWEn,
  input  clk,
  output [31:0] ra,
  output [31:0] sp,
  output [31:0] t0,
  output [31:0] t1,
  output [31:0] t2,
  output [31:0] s0,
  output [31:0] s1,
  output [31:0] a0,
  output [31:0] ReadData1,
  output [31:0] ReadData2
);

  wire v0, v1, v2, v3, v4, v5, v6, v7, v8, v9, v10, v11, v12, v13, v14, v15, v16, v17, v18, v19, v20, v21,
       v22, v23, v24, v25, v26, v27, v28, v29, v30, v31;
  wire [31:0] a1, a2, a3, a4, a5, a6, a7, gp, s2, s3, s4, s5, s6, s7, s8, s9, s10, s11, t3, t4, t5, t6, tp;

  Multiplexer #(.select(5), .width(32)) multiplexer_1 (
    .in0({32{1'b0}}), .in1(ra), .in2(sp), .in3(gp), .in4(tp), .in5(t0), .in6(t1), .in7(t2), .in8(s0),
    .in9(s1), .in10(a0), .in11(a1), .in12(a2), .in13(a3), .in14(a4), .in15(a5), .in16(a6), .in17(a7),
    .in18(s2), .in19(s3), .in20(s4), .in21(s5), .in22(s6), .in23(s7), .in24(s8), .in25(s9), .in26(s10),
    .in27(s11), .in28(t3), .in29(t4), .in30(t5), .in31(t6), .out(ReadData1), .sel(ReadIndex1));
  Demultiplexer #(.select(5)) demultiplexer_1 (
    .out0(v0), .out1(v1), .out2(v2), .out3(v3), .out4(v4), .out5(v5), .out6(v6), .out7(v7), .out8(v8),
    .out9(v9), .out10(v10), .out11(v11), .out12(v12), .out13(v13), .out14(v14), .out15(v15), .out16(v16),
    .out17(v17), .out18(v18), .out19(v19), .out20(v20), .out21(v21), .out22(v22), .out23(v23), .out24(v24),
    .out25(v25), .out26(v26), .out27(v27), .out28(v28), .out29(v29), .out30(v30), .out31(v31), .in(RegWEn),
    .sel(WriteIndex));
  Multiplexer #(.select(5), .width(32)) multiplexer_2 (
    .in0({32{1'b0}}), .in1(ra), .in2(sp), .in3(gp), .in4(tp), .in5(t0), .in6(t1), .in7(t2), .in8(s0),
    .in9(s1), .in10(a0), .in11(a1), .in12(a2), .in13(a3), .in14(a4), .in15(a5), .in16(a6), .in17(a7),
    .in18(s2), .in19(s3), .in20(s4), .in21(s5), .in22(s6), .in23(s7), .in24(s8), .in25(s9), .in26(s10),
    .in27(s11), .in28(t3), .in29(t4), .in30(t5), .in31(t6), .out(ReadData2), .sel(ReadIndex2));
  Register #(.width(32)) register_1 (.D(WriteData), .en(v1), .Q(ra), .clk(clk));  // open: clr
  Register #(.width(32)) register_2 (.D(WriteData), .en(v2), .Q(sp), .clk(clk));  // open: clr
  Register #(.width(32)) register_3 (.D(WriteData), .en(v3), .Q(gp), .clk(clk));  // open: clr
  Register #(.width(32)) register_4 (.D(WriteData), .en(v4), .Q(tp), .clk(clk));  // open: clr
  Register #(.width(32)) register_5 (.D(WriteData), .en(v25), .Q(s9), .clk(clk));  // open: clr
  Register #(.width(32)) register_6 (.D(WriteData), .en(v26), .Q(s10), .clk(clk));  // open: clr
  Register #(.width(32)) register_7 (.D(WriteData), .en(v27), .Q(s11), .clk(clk));  // open: clr
  Register #(.width(32)) register_8 (.D(WriteData), .en(v28), .Q(t3), .clk(clk));  // open: clr
  Register #(.width(32)) register_9 (.D(WriteData), .en(v5), .Q(t0), .clk(clk));  // open: clr
  Register #(.width(32)) register_10 (.D(WriteData), .en(v6), .Q(t1), .clk(clk));  // open: clr
  Register #(.width(32)) register_11 (.D(WriteData), .en(v7), .Q(t2), .clk(clk));  // open: clr
  Register #(.width(32)) register_12 (.D(WriteData), .en(v8), .Q(s0), .clk(clk));  // open: clr
  Register #(.width(32)) register_13 (.D(WriteData), .en(v29), .Q(t4), .clk(clk));  // open: clr
  Register #(.width(32)) register_14 (.D(WriteData), .en(v30), .Q(t5), .clk(clk));  // open: clr
  Register #(.width(32)) register_15 (.D(WriteData), .en(v31), .Q(t6), .clk(clk));  // open: clr
  Register #(.width(32)) register_16 (.D(WriteData), .en(v9), .Q(s1), .clk(clk));  // open: clr
  Register #(.width(32)) register_17 (.D(WriteData), .en(v10), .Q(a0), .clk(clk));  // open: clr
  Register #(.width(32)) register_18 (.D(WriteData), .en(v11), .Q(a1), .clk(clk));  // open: clr
  Register #(.width(32)) register_19 (.D(WriteData), .en(v12), .Q(a2), .clk(clk));  // open: clr
  Register #(.width(32)) register_20 (.D(WriteData), .en(v13), .Q(a3), .clk(clk));  // open: clr
  Register #(.width(32)) register_21 (.D(WriteData), .en(v14), .Q(a4), .clk(clk));  // open: clr
  Register #(.width(32)) register_22 (.D(WriteData), .en(v15), .Q(a5), .clk(clk));  // open: clr
  Register #(.width(32)) register_23 (.D(WriteData), .en(v16), .Q(a6), .clk(clk));  // open: clr
  Register #(.width(32)) register_24 (.D(WriteData), .en(v17), .Q(a7), .clk(clk));  // open: clr
  Register #(.width(32)) register_25 (.D(WriteData), .en(v18), .Q(s2), .clk(clk));  // open: clr
  Register #(.width(32)) register_26 (.D(WriteData), .en(v19), .Q(s3), .clk(clk));  // open: clr
  Register #(.width(32)) register_27 (.D(WriteData), .en(v20), .Q(s4), .clk(clk));  // open: clr
  Register #(.width(32)) register_28 (.D(WriteData), .en(v21), .Q(s5), .clk(clk));  // open: clr
  Register #(.width(32)) register_29 (.D(WriteData), .en(v22), .Q(s6), .clk(clk));  // open: clr
  Register #(.width(32)) register_30 (.D(WriteData), .en(v23), .Q(s7), .clk(clk));  // open: clr
  Register #(.width(32)) register_31 (.D(WriteData), .en(v24), .Q(s8), .clk(clk));  // open: clr

  // Notes on the sheet:
  //   INPUTS to your circuit
  //   DON'T CHANGE THE LOCATIONS OF THE INPUTS AND OUTPUTS!
  //   These are DEBUG/TEST outputs from your circuit.
  //   OUTPUTS from your circuit
endmodule
